// Logisim project 16 Bit ALU.circ as structural Verilog: 4 circuits, main circuit Regisor_File
module Regisor_File (
  input  [3:0] Read_Reg_1,
  input  [15:0] Data_Input,
  input  [3:0] write_reg,
  input  Clock,
  input  enable,
  input  [3:0] Read_reg_2,
  output [15:0] Read_data_1,
  output [15:0] Read_Data_2
);

  wire decoder_1_out0, decoder_1_out1, decoder_1_out2, decoder_1_out3, decoder_1_out4, decoder_1_out5,
       decoder_1_out6, decoder_1_out7, decoder_1_out8, decoder_1_out9, decoder_1_out10, decoder_1_out11,
       decoder_1_out12, decoder_1_out13, decoder_1_out14, decoder_1_out15;
  wire [15:0] register_1_q, register_2_q, register_3_q, register_4_q, register_5_q, register_6_q,
       register_7_q, register_8_q, register_9_q, register_10_q, register_11_q, register_12_q, register_13_q,
       register_14_q, register_15_q, register_16_q;

  Decoder #(.select(4)) decoder_1 (
    .out0(decoder_1_out0), .out1(decoder_1_out1), .out2(decoder_1_out2), .out3(decoder_1_out3),
    .out4(decoder_1_out4), .out5(decoder_1_out5), .out6(decoder_1_out6), .out7(decoder_1_out7),
    .out8(decoder_1_out8), .out9(decoder_1_out9), .out10(decoder_1_out10), .out11(decoder_1_out11),
    .out12(decoder_1_out12), .out13(decoder_1_out13), .out14(decoder_1_out14), .out15(decoder_1_out15),
    .sel(write_reg), .en(enable));
  Register #(.width(16)) register_1 (.D(Data_Input), .en(decoder_1_out0), .clk(Clock), .Q(register_1_q));  // open: clr
  Register #(.width(16)) register_2 (.D(Data_Input), .en(decoder_1_out1), .clk(Clock), .Q(register_2_q));  // open: clr
  Register #(.width(16)) register_3 (.D(Data_Input), .en(decoder_1_out2), .clk(Clock), .Q(register_3_q));  // open: clr
  Register #(.width(16)) register_4 (.D(Data_Input), .en(decoder_1_out3), .clk(Clock), .Q(register_4_q));  // open: clr
  Register #(.width(16)) register_5 (.D(Data_Input), .en(decoder_1_out4), .clk(Clock), .Q(register_5_q));  // open: clr
  Register #(.width(16)) register_6 (.D(Data_Input), .en(decoder_1_out5), .clk(Clock), .Q(register_6_q));  // open: clr
  Register #(.width(16)) register_7 (.D(Data_Input), .en(decoder_1_out6), .clk(Clock), .Q(register_7_q));  // open: clr
  Register #(.width(16)) register_8 (.D(Data_Input), .en(decoder_1_out7), .clk(Clock), .Q(register_8_q));  // open: clr
  Register #(.width(16)) register_9 (.D(Data_Input), .en(decoder_1_out8), .clk(Clock), .Q(register_9_q));  // open: clr
  Register #(.width(16)) register_10 (
    .D(Data_Input), .en(decoder_1_out9), .clk(Clock), .Q(register_10_q));  // open: clr
  Register #(.width(16)) register_11 (
    .D(Data_Input), .en(decoder_1_out10), .clk(Clock), .Q(register_11_q));  // open: clr
  Register #(.width(16)) register_12 (
    .D(Data_Input), .en(decoder_1_out11), .clk(Clock), .Q(register_12_q));  // open: clr
  Register #(.width(16)) register_13 (
    .D(Data_Input), .en(decoder_1_out12), .clk(Clock), .Q(register_13_q));  // open: clr
  Register #(.width(16)) register_14 (
    .D(Data_Input), .en(decoder_1_out13), .clk(Clock), .Q(register_14_q));  // open: clr
  Register #(.width(16)) register_15 (
    .D(Data_Input), .en(decoder_1_out14), .clk(Clock), .Q(register_15_q));  // open: clr
  Register #(.width(16)) register_16 (
    .D(Data_Input), .en(decoder_1_out15), .clk(Clock), .Q(register_16_q));  // open: clr
  Multiplexer #(.select(4), .width(16)) multiplexer_1 (
    .in0(register_1_q), .in1(register_2_q), .in2(register_3_q), .in3(register_4_q), .in4(register_5_q),
    .in5(register_6_q), .in6(register_7_q), .in7(register_8_q), .in8(register_9_q), .in9(register_10_q),
    .in10(register_11_q), .in11(register_12_q), .in12(register_13_q), .in13(register_14_q),
    .in14(register_15_q), .in15(register_16_q), .out(Read_data_1), .sel(Read_Reg_1));
  Multiplexer #(.select(4), .width(16)) multiplexer_2 (
    .in0(register_1_q), .in1(register_2_q), .in2(register_3_q), .in3(register_4_q), .in4(register_5_q),
    .in5(register_6_q), .in6(register_7_q), .in7(register_8_q), .in8(register_9_q), .in9(register_10_q),
    .in10(register_11_q), .in11(register_12_q), .in12(register_13_q), .in13(register_14_q),
    .in14(register_15_q), .in15(register_16_q), .out(Read_Data_2), .sel(Read_reg_2));
endmodule

module R_Type_datapath (
  input  [15:0] in_1,
  input  Cin,
  input  B_Inv,
  input  [2:0] OpCode,
  input  in_5,
  output [15:0] reg1,
  output [15:0] reg2,
  output [3:0] op_code,
  output [3:0] RD,
  output [3:0] RT,
  output [3:0] RS,
  output [15:0] Output1,
  output Ovr_Flow
);

  wire Clk_out;
  wire [15:0] adder_1_out, register_1_q;

  Clock Clk (.out(Clk_out));
  Register #(.width(16)) register_1 (.D(adder_1_out), .clk(Clk_out), .Q(register_1_q));  // open: en, clr
  ROM #(.addrWidth(16), .dataWidth(16)) rom_1 (.addr(register_1_q), .data({op_code, RS, RT, RD}));
  Adder #(.width(16)) adder_1 (.a(register_1_q), .b(in_1), .out(adder_1_out));  // open: cin, cout
  Regisor_File regisor_file_1 (
    .Read_Reg_1(RT), .Read_reg_2(RS), .Clock(Clk_out), .enable(in_5), .write_reg(RD), .Data_Input(Output1),
    .Read_data_1(reg1), .Read_Data_2(reg2));
  alu_16bit alu_16bit_1 (
    .B5(reg2[4]), .B6(reg2[5]), .B7(reg2[6]), .B8(reg2[7]), .B9(reg2[8]), .B10(reg2[9]), .B11(reg2[10]),
    .B12(reg2[11]), .B13(reg2[12]), .B14(reg2[13]), .A1(reg1[0]), .B15(reg2[14]), .B16(reg2[15]),
    .A2(reg1[1]), .A3(reg1[2]), .A4(reg1[3]), .A5(reg1[4]), .A6(reg1[5]), .A7(reg1[6]), .A8(reg1[7]),
    .A9(reg1[8]), .Cin(Cin), .A10(reg1[9]), .A11(reg1[10]), .A12(reg1[11]), .A13(reg1[12]), .A14(reg1[13]),
    .A15(reg1[14]), .A16(reg1[15]), .B1(reg2[0]), .B2(reg2[1]), .B_inv(B_Inv), .B3(reg2[2]), .B4(reg2[3]),
    .Op_Code(OpCode), .R1(Output1[0]), .R2(Output1[1]), .R3(Output1[2]), .R4(Output1[3]), .R5(Output1[4]),
    .R6(Output1[5]), .R7(Output1[6]), .R8(Output1[7]), .R9(Output1[8]), .R10(Output1[9]), .R11(Output1[10]),
    .R12(Output1[11]), .R13(Output1[12]), .R14(Output1[13]), .R15(Output1[14]), .R16(Output1[15]),
    .Over_Flow(Ovr_Flow));

  // Notes on the sheet:
  //   contents of rom_1 (hex, n*v repeats v):
  //   19*0 1 2
endmodule

module alu_1bit (
  input  A,
  input  B,
  input  B_Inv,
  input  Cin,
  input  [2:0] ALU_OP,
  output Cout,
  output RES
);

  wire adder_1_out, and_1_out, multiplexer_1_out, nand_1_out, not_1_out, or_1_out, shifter_1_out,
       shifter_2_out, xnor_1_out, xor_1_out;

  Multiplexer multiplexer_1 (.in0(B), .in1(not_1_out), .out(multiplexer_1_out), .sel(B_Inv));
  not not_1 (not_1_out, B);
  and and_1 (and_1_out, A, B);
  or or_1 (or_1_out, A, B);
  Adder #(.width(1)) adder_1 (.a(A), .b(multiplexer_1_out), .out(adder_1_out), .cin(Cin), .cout(Cout));
  xor xor_1 (xor_1_out, A, B);
  nand nand_1 (nand_1_out, A, B);
  xnor xnor_1 (xnor_1_out, A, B);
  Shifter #(.width(1)) shifter_1 (.in(A), .\dist (B), .out(shifter_1_out));
  Shifter #(.width(1)) shifter_2 (.in(A), .\dist (B), .out(shifter_2_out));
  Multiplexer #(.select(3)) multiplexer_2 (
    .in0(and_1_out), .in1(or_1_out), .in2(adder_1_out), .in3(xor_1_out), .in4(nand_1_out), .in5(xnor_1_out),
    .in6(shifter_1_out), .in7(shifter_2_out), .out(RES), .sel(ALU_OP));
endmodule

module alu_16bit (
  input  Cin,
  input  [2:0] Op_Code,
  input  B_inv,
  input  A1,
  input  A2,
  input  A3,
  input  A4,
  input  A5,
  input  A6,
  input  A7,
  input  A8,
  input  A9,
  input  A10,
  input  A11,
  input  A12,
  input  A13,
  input  A14,
  input  A15,
  input  A16,
  input  B1,
  input  B2,
  input  B3,
  input  B4,
  input  B5,
  input  B6,
  input  B7,
  input  B8,
  input  B9,
  input  B10,
  input  B11,
  input  B12,
  input  B13,
  input  B14,
  input  B15,
  input  B16,
  output R1,
  output R2,
  output R3,
  output R4,
  output R5,
  output R6,
  output R7,
  output R8,
  output R9,
  output R10,
  output R11,
  output R12,
  output R13,
  output R14,
  output R15,
  output R16,
  output Over_Flow
);

  wire alu_1bit_1_cout, alu_1bit_2_cout, alu_1bit_3_cout, alu_1bit_4_cout, alu_1bit_5_cout, alu_1bit_6_cout,
       alu_1bit_7_cout, alu_1bit_8_cout, alu_1bit_9_cout, alu_1bit_10_cout, alu_1bit_11_cout,
       alu_1bit_12_cout, alu_1bit_13_cout, alu_1bit_14_cout, alu_1bit_15_cout;

  alu_1bit alu_1bit_1 (.Cin(Cin), .B_Inv(B_inv), .B(B1), .A(A1), .ALU_OP(Op_Code), .Cout(alu_1bit_1_cout), .RES(R1));
  alu_1bit alu_1bit_2 (
    .Cin(alu_1bit_1_cout), .B_Inv(B_inv), .B(B2), .A(A2), .ALU_OP(Op_Code), .Cout(alu_1bit_2_cout), .RES(R2));
  alu_1bit alu_1bit_3 (
    .Cin(alu_1bit_2_cout), .B_Inv(B_inv), .B(B3), .A(A3), .ALU_OP(Op_Code), .Cout(alu_1bit_3_cout), .RES(R3));
  alu_1bit alu_1bit_4 (
    .Cin(alu_1bit_3_cout), .B_Inv(B_inv), .B(B4), .A(A4), .ALU_OP(Op_Code), .Cout(alu_1bit_4_cout), .RES(R4));
  alu_1bit alu_1bit_5 (
    .Cin(alu_1bit_4_cout), .B_Inv(B_inv), .B(B5), .A(A5), .ALU_OP(Op_Code), .Cout(alu_1bit_5_cout), .RES(R5));
  alu_1bit alu_1bit_6 (
    .Cin(alu_1bit_5_cout), .B_Inv(B_inv), .B(B6), .A(A6), .ALU_OP(Op_Code), .Cout(alu_1bit_6_cout), .RES(R6));
  alu_1bit alu_1bit_7 (
    .Cin(alu_1bit_6_cout), .B_Inv(B_inv), .B(B7), .A(A7), .ALU_OP(Op_Code), .Cout(alu_1bit_7_cout), .RES(R7));
  alu_1bit alu_1bit_8 (
    .Cin(alu_1bit_7_cout), .B_Inv(B_inv), .B(B8), .A(A8), .ALU_OP(Op_Code), .Cout(alu_1bit_8_cout), .RES(R8));
  alu_1bit alu_1bit_9 (
    .Cin(alu_1bit_8_cout), .B_Inv(B_inv), .B(B9), .A(A9), .ALU_OP(Op_Code), .Cout(alu_1bit_9_cout), .RES(R9));
  alu_1bit alu_1bit_10 (
    .Cin(alu_1bit_9_cout), .B_Inv(B_inv), .B(B10), .A(A10), .ALU_OP(Op_Code), .Cout(alu_1bit_10_cout),
    .RES(R10));
  alu_1bit alu_1bit_11 (
    .Cin(alu_1bit_10_cout), .B_Inv(B_inv), .B(B11), .A(A11), .ALU_OP(Op_Code), .Cout(alu_1bit_11_cout),
    .RES(R11));
  alu_1bit alu_1bit_12 (
    .Cin(alu_1bit_11_cout), .B_Inv(B_inv), .B(B12), .A(A12), .ALU_OP(Op_Code), .Cout(alu_1bit_12_cout),
    .RES(R12));
  alu_1bit alu_1bit_13 (
    .Cin(alu_1bit_12_cout), .B_Inv(B_inv), .B(B13), .A(A13), .ALU_OP(Op_Code), .Cout(alu_1bit_13_cout),
    .RES(R13));
  alu_1bit alu_1bit_14 (
    .Cin(alu_1bit_13_cout), .B_Inv(B_inv), .B(B14), .A(A14), .ALU_OP(Op_Code), .Cout(alu_1bit_14_cout),
    .RES(R14));
  alu_1bit alu_1bit_15 (
    .Cin(alu_1bit_14_cout), .B_Inv(B_inv), .B(B15), .A(A15), .ALU_OP(Op_Code), .Cout(alu_1bit_15_cout),
    .RES(R15));
  alu_1bit alu_1bit_16 (
    .Cin(alu_1bit_15_cout), .B_Inv(B_inv), .B(B16), .A(A16), .ALU_OP(Op_Code), .Cout(Over_Flow), .RES(R16));
endmodule
