// Logisim project Full-Datapath.circ as structural Verilog
module Register_File (
  input  [3:0] Read_Reg_1,
  input  [11:0] Data_Input,
  input  [3:0] write_reg,
  input  Clock,
  input  enable,
  input  [3:0] Read_reg_2,
  output [11:0] Read_data_1,
  output [11:0] Read_Data_2
);

  wire decoder_1_out0, decoder_1_out1, decoder_1_out2, decoder_1_out3, decoder_1_out4, decoder_1_out5,
       decoder_1_out6, decoder_1_out7, decoder_1_out8, decoder_1_out9, decoder_1_out10, decoder_1_out11,
       decoder_1_out12, decoder_1_out13, decoder_1_out14, decoder_1_out15;
  wire [11:0] register_1_q, register_2_q, register_3_q, register_4_q, register_5_q, register_6_q,
       register_7_q, register_8_q, register_9_q, register_10_q, register_11_q, register_12_q, register_13_q,
       register_14_q, register_15_q, register_16_q;

  Decoder #(.select(4)) decoder_1 (
    .out0(decoder_1_out0), .out1(decoder_1_out1), .out2(decoder_1_out2), .out3(decoder_1_out3),
    .out4(decoder_1_out4), .out5(decoder_1_out5), .out6(decoder_1_out6), .out7(decoder_1_out7),
    .out8(decoder_1_out8), .out9(decoder_1_out9), .out10(decoder_1_out10), .out11(decoder_1_out11),
    .out12(decoder_1_out12), .out13(decoder_1_out13), .out14(decoder_1_out14), .out15(decoder_1_out15),
    .sel(write_reg), .en(enable));
  Register #(.width(12)) register_1 (.D(Data_Input), .en(decoder_1_out0), .clk(Clock), .Q(register_1_q));  // open: clr
  Register #(.width(12)) register_2 (.D(Data_Input), .en(decoder_1_out1), .clk(Clock), .Q(register_2_q));  // open: clr
  Register #(.width(12)) register_3 (.D(Data_Input), .en(decoder_1_out2), .clk(Clock), .Q(register_3_q));  // open: clr
  Register #(.width(12)) register_4 (.D(Data_Input), .en(decoder_1_out3), .clk(Clock), .Q(register_4_q));  // open: clr
  Register #(.width(12)) register_5 (.D(Data_Input), .en(decoder_1_out4), .clk(Clock), .Q(register_5_q));  // open: clr
  Register #(.width(12)) register_6 (.D(Data_Input), .en(decoder_1_out5), .clk(Clock), .Q(register_6_q));  // open: clr
  Register #(.width(12)) register_7 (.D(Data_Input), .en(decoder_1_out6), .clk(Clock), .Q(register_7_q));  // open: clr
  Register #(.width(12)) register_8 (.D(Data_Input), .en(decoder_1_out7), .clk(Clock), .Q(register_8_q));  // open: clr
  Register #(.width(12)) register_9 (.D(Data_Input), .en(decoder_1_out8), .clk(Clock), .Q(register_9_q));  // open: clr
  Register #(.width(12)) register_10 (
    .D(Data_Input), .en(decoder_1_out9), .clk(Clock), .Q(register_10_q));  // open: clr
  Register #(.width(12)) register_11 (
    .D(Data_Input), .en(decoder_1_out10), .clk(Clock), .Q(register_11_q));  // open: clr
  Register #(.width(12)) register_12 (
    .D(Data_Input), .en(decoder_1_out11), .clk(Clock), .Q(register_12_q));  // open: clr
  Register #(.width(12)) register_13 (
    .D(Data_Input), .en(decoder_1_out12), .clk(Clock), .Q(register_13_q));  // open: clr
  Register #(.width(12)) register_14 (
    .D(Data_Input), .en(decoder_1_out13), .clk(Clock), .Q(register_14_q));  // open: clr
  Register #(.width(12)) register_15 (
    .D(Data_Input), .en(decoder_1_out14), .clk(Clock), .Q(register_15_q));  // open: clr
  Register #(.width(12)) register_16 (
    .D(Data_Input), .en(decoder_1_out15), .clk(Clock), .Q(register_16_q));  // open: clr
  Multiplexer #(.select(4), .width(12)) multiplexer_1 (
    .in0(register_1_q), .in1(register_2_q), .in2(register_3_q), .in3(register_4_q), .in4(register_5_q),
    .in5(register_6_q), .in6(register_7_q), .in7(register_8_q), .in8(register_9_q), .in9(register_10_q),
    .in10(register_11_q), .in11(register_12_q), .in12(register_13_q), .in13(register_14_q),
    .in14(register_15_q), .in15(register_16_q), .out(Read_data_1), .sel(Read_Reg_1));
  Multiplexer #(.select(4), .width(12)) multiplexer_2 (
    .in0(register_1_q), .in1(register_2_q), .in2(register_3_q), .in3(register_4_q), .in4(register_5_q),
    .in5(register_6_q), .in6(register_7_q), .in7(register_8_q), .in8(register_9_q), .in9(register_10_q),
    .in10(register_11_q), .in11(register_12_q), .in12(register_13_q), .in13(register_14_q),
    .in14(register_15_q), .in15(register_16_q), .out(Read_Data_2), .sel(Read_reg_2));
endmodule

module R_Type_datapath (
  input  [15:0] in_1,
  input  [2:0] in_2,
  input  in_3,
  input  in_4,
  input  in_5,
  output [11:0] reg1,
  output [11:0] reg2,
  output [3:0] op_code,
  output [3:0] RD,
  output [3:0] RT,
  output [11:0] Output1,
  output [3:0] RS,
  output out_13
);

  wire Clk_out;
  wire [3:3] undriven;
  wire [15:0] adder_1_out, register_1_q;

  Clock Clk (.out(Clk_out));
  Register #(.width(16)) register_1 (.D(adder_1_out), .clk(Clk_out), .Q(register_1_q));  // open: en, clr
  ROM #(.addrWidth(16), .dataWidth(16)) rom_1 (.addr(register_1_q), .data({op_code, RS, RT, RD}));
  Adder #(.width(16)) adder_1 (.a(register_1_q), .b(in_1), .out(adder_1_out));  // open: cin, cout
  Register_File register_file_1 (
    .Read_Reg_1(RT), .Read_reg_2(RS), .Clock(Clk_out), .enable(in_5), .Data_Input(Output1), .write_reg(RD),
    .Read_data_1(reg1), .Read_Data_2(reg2));
  alu alu_1 (
    .Cin(in_4), .B_Inv(in_3), .A(reg1), .B(reg2), .ALU_OP({undriven[3], in_2}), .out_6(out_13), .RES(Output1));  // open: zero
  // Pins of 3 and 4 bits meet at {undriven[3], in_2}

  // Notes on the sheet:
  //   contents of rom_1 (hex, n*v repeats v):
  //   4345 6348 789 16*0 1 2
endmodule

module alu (
  input  [11:0] A,
  input  [11:0] B,
  input  B_Inv,
  input  Cin,
  input  [3:0] ALU_OP,
  output out_6,
  output [11:0] RES,
  output zero
);

  wire comparator_1_lt;
  wire [11:0] adder_1_out, and_1_out, bit_extender_1_out, multiplexer_1_out, nand_1_out, not_1_out,
       not_2_out, or_1_out, shifter_1_out, shifter_2_out, xnor_1_out, xor_1_out;

  assign not_1_out = ~B;  // NOT_Gate not_1, 12 bits wide
  assign and_1_out = A & B;  // AND_Gate and_1, 12 bits wide
  assign or_1_out = A | B;  // OR_Gate or_1, 12 bits wide
  Adder #(.width(12)) adder_1 (.a(A), .b(multiplexer_1_out), .out(adder_1_out), .cin(Cin), .cout(out_6));
  Multiplexer #(.width(12)) multiplexer_1 (.in0(B), .in1(not_1_out), .out(multiplexer_1_out), .sel(B_Inv));
  Shifter #(.width(12)) shifter_1 (.in(A), .\dist (B[11:8]), .out(shifter_1_out));
  assign not_2_out = ~B;  // NOT_Gate not_2, 12 bits wide
  assign xor_1_out = A ^ B;  // XOR_Gate xor_1, 12 bits wide
  assign nand_1_out = ~(A & B);  // NAND_Gate nand_1, 12 bits wide
  assign xnor_1_out = ~(A ^ B);  // XNOR_Gate xnor_1, 12 bits wide
  Shifter #(.shift("lr"), .width(12)) shifter_2 (.in(A), .\dist (B[11:8]), .out(shifter_2_out));
  Comparator #(.width(12)) comparator_1 (.a(A), .b(B), .lt(comparator_1_lt));  // open: gt, eq
  assign bit_extender_1_out = {{11{comparator_1_lt}}, comparator_1_lt};  // Bit_Extender bit_extender_1
  Multiplexer #(.select(4), .width(12)) multiplexer_2 (
    .in0(and_1_out), .in1(or_1_out), .in2(adder_1_out), .in3(xor_1_out), .in4(nand_1_out), .in5(xnor_1_out),
    .in6(shifter_1_out), .in7(not_2_out), .in8(shifter_2_out), .in9(bit_extender_1_out), .out(RES),
    .sel(ALU_OP));  // open: in10, in11, in12, in13, in14, in15
  nor nor_1 (zero, RES[0], RES[1], RES[2], RES[3], RES[4], RES[5], RES[7], RES[8], RES[9], RES[10], RES[11], RES[6]);
endmodule

module i_type_datapath (
  input  [15:0] Plus_1,
  input  B_Inv,
  input  [2:0] Alu_Op,
  input  in_4,
  input  in_5,
  output [11:0] reg1,
  output [11:0] reg2,
  output [3:0] op_code,
  output [3:0] Immediate,
  output [3:0] Dest,
  output [11:0] Output1,
  output [3:0] Source,
  output Over_Flow
);

  wire Clk_out;
  wire [3:3] undriven;
  wire [11:0] bit_extender_1_out;
  wire [15:0] adder_1_out, register_1_q;

  Clock Clk (.out(Clk_out));
  Register #(.width(16)) register_1 (.D(adder_1_out), .clk(Clk_out), .Q(register_1_q));  // open: en, clr
  ROM #(.addrWidth(16), .dataWidth(16)) rom_1 (.addr(register_1_q), .data({op_code, Source, Dest, Immediate}));
  Adder #(.width(16)) adder_1 (.a(register_1_q), .b(Plus_1), .out(adder_1_out));  // open: cin, cout
  Register_File register_file_1 (
    .Read_Reg_1(Source), .Clock(Clk_out), .enable(in_5), .Data_Input(Output1), .write_reg(Dest),
    .Read_data_1(reg1), .Read_Data_2(reg2));  // open: Read_reg_2
  assign bit_extender_1_out = {{8{1'b0}}, Immediate};  // Bit_Extender bit_extender_1
  alu alu_1 (
    .Cin(in_4), .B_Inv(B_Inv), .A(reg1), .B(bit_extender_1_out), .ALU_OP({undriven[3], Alu_Op}),
    .out_6(Over_Flow), .RES(Output1));  // open: zero
  // Pins of 3 and 4 bits meet at {undriven[3], Alu_Op}

  // Notes on the sheet:
  //   contents of rom_1 (hex, n*v repeats v):
  //   4345 18*0 1 2
endmodule

module load_type (
  input  [15:0] in_1,
  input  [2:0] in_2,
  input  in_3,
  input  in_4,
  input  in_5,
  input  in_6,
  input  in_7,
  output [11:0] reg1,
  output [11:0] reg2,
  output [3:0] op_code,
  output [3:0] Immediate,
  output [3:0] Destination,
  output [11:0] Output1,
  output [3:0] Base,
  output out_15
);

  wire Clk_out;
  wire [3:3] undriven_2;
  wire [11:0] alu_1_res, bit_extender_1_out, undriven;
  wire [15:0] adder_1_out, register_1_q;

  Clock Clk (.out(Clk_out));
  Register #(.width(16)) register_1 (.D(adder_1_out), .clk(Clk_out), .Q(register_1_q));  // open: en, clr
  ROM #(.addrWidth(16), .dataWidth(16)) rom_1 (.addr(register_1_q), .data({op_code, Base, Destination, Immediate}));
  Adder #(.width(16)) adder_1 (.a(register_1_q), .b(in_1), .out(adder_1_out));  // open: cin, cout
  Register_File register_file_1 (
    .Read_Reg_1(Base), .Clock(Clk_out), .enable(in_5), .Data_Input(Output1), .write_reg(Destination),
    .Read_data_1(reg1), .Read_Data_2(reg2));  // open: Read_reg_2
  assign bit_extender_1_out = {{8{Immediate[3]}}, Immediate};  // Bit_Extender bit_extender_1
  RAM #(.addrWidth(12), .asyncread("true"), .dataWidth(12)) ram_1 (
    .addr(alu_1_res), .we(in_6), .oe(in_7), .clk(Clk_out), .din(undriven), .dout(Output1));
  alu alu_1 (
    .Cin(in_4), .B_Inv(in_3), .A(reg1), .B(bit_extender_1_out), .ALU_OP({undriven_2[3], in_2}),
    .out_6(out_15), .RES(alu_1_res));  // open: zero
  // Pins of 3 and 4 bits meet at {undriven_2[3], in_2}

  // Notes on the sheet:
  //   contents of rom_1 (hex, n*v repeats v):
  //   4345 6348 789 16*0 1 2
endmodule

module store_type (
  input  [15:0] in_1,
  input  [2:0] in_2,
  input  in_3,
  input  in_4,
  input  in_5,
  input  in_6,
  input  in_7,
  output [11:0] reg1,
  output [11:0] reg2,
  output [3:0] op_code,
  output [3:0] RD,
  output [3:0] RT,
  output [11:0] Output1,
  output [3:0] RS,
  output out_15
);

  wire Clk_out;
  wire [3:0] undriven;
  wire [3:3] undriven_2;
  wire [11:0] alu_1_res, bit_extender_1_out;
  wire [15:0] adder_1_out, register_1_q;

  Clock Clk (.out(Clk_out));
  Register #(.width(16)) register_1 (.D(adder_1_out), .clk(Clk_out), .Q(register_1_q));  // open: en, clr
  ROM #(.addrWidth(16), .dataWidth(16)) rom_1 (.addr(register_1_q), .data({op_code, RS, RT, RD}));
  Adder #(.width(16)) adder_1 (.a(register_1_q), .b(in_1), .out(adder_1_out));  // open: cin, cout
  Register_File register_file_1 (
    .Read_Reg_1(RS), .Read_reg_2(undriven), .Clock(Clk_out), .enable(in_5), .Data_Input(Output1),
    .Read_data_1(reg1), .Read_Data_2(reg2));  // open: write_reg
  assign bit_extender_1_out = {{8{RD[3]}}, RD};  // Bit_Extender bit_extender_1
  RAM #(.addrWidth(12), .asyncread("true"), .dataWidth(12)) ram_1 (
    .addr(alu_1_res), .we(in_6), .oe(in_7), .clk(Clk_out), .din(reg2));  // open: dout
  alu alu_1 (
    .Cin(in_4), .B_Inv(in_3), .A(reg1), .B(bit_extender_1_out), .ALU_OP({undriven_2[3], in_2}),
    .out_6(out_15), .RES(alu_1_res));  // open: zero
  // Pins of 3 and 4 bits meet at {undriven_2[3], in_2}

  // Notes on the sheet:
  //   contents of rom_1 (hex, n*v repeats v):
  //   4345 6348 789 16*0 1 2
endmodule

module Control_Unit (
  input  [3:0] Opcode,
  output [3:0] Def_Reg,
  output RegWrite,
  output AluSrc,
  output [3:0] AluOp,
  output Cin,
  output Bin,
  output Lw,
  output Sw,
  output RamToReg,
  output Read_Dest,
  output Add_Br,
  output Jump,
  output Inp,
  output Outp,
  output [3:0] Sll2
);

  wire and_1_out, and_2_out, and_3_out, and_4_out, and_5_out, and_6_out, and_7_out, and_8_out, and_9_out,
       and_10_out, and_11_out, and_12_out, and_13_out, and_14_out, and_15_out, and_16_out, and_17_out,
       and_18_out, and_19_out, and_20_out, and_21_out, and_25_out, and_26_out, and_27_out, and_28_out,
       and_29_out, not_1_out, not_2_out, not_3_out, not_4_out;

  not not_1 (not_1_out, Opcode[3]);
  not not_2 (not_2_out, Opcode[2]);
  not not_3 (not_3_out, Opcode[1]);
  not not_4 (not_4_out, Opcode[0]);
  and and_1 (and_1_out, not_2_out, not_3_out, Opcode[0]);
  and and_2 (and_2_out, Opcode[2], Opcode[1], Opcode[0]);
  and and_3 (and_3_out, Opcode[1], not_4_out);
  and and_4 (and_4_out, not_1_out, Opcode[2], Opcode[0]);
  and and_5 (and_5_out, Opcode[3], not_2_out, not_3_out);
  and and_6 (and_6_out, Opcode[2], not_3_out, Opcode[0]);
  and and_7 (and_7_out, not_1_out, Opcode[2], Opcode[1], not_4_out);
  and and_8 (and_8_out, Opcode[3], Opcode[2], not_3_out);
  and and_9 (and_9_out, not_1_out, Opcode[2], not_3_out, Opcode[0]);
  and and_10 (and_10_out, Opcode[3], Opcode[2], Opcode[1], Opcode[0]);
  and and_11 (and_11_out, not_1_out, not_2_out, not_4_out);
  and and_12 (and_12_out, not_2_out, not_3_out, not_4_out);
  and and_13 (and_13_out, Opcode[3], Opcode[1], Opcode[0]);
  and and_14 (and_14_out, not_1_out, not_3_out, Opcode[0]);
  and and_15 (and_15_out, not_1_out, Opcode[2], Opcode[0]);
  and and_16 (and_16_out, not_1_out, Opcode[2], not_3_out, not_4_out);
  and and_17 (and_17_out, Opcode[3], Opcode[2], Opcode[1], Opcode[0]);
  and and_18 (and_18_out, not_1_out, not_2_out, not_3_out, Opcode[0]);
  and and_19 (and_19_out, Opcode[3], not_2_out, Opcode[1], Opcode[0]);
  and and_20 (and_20_out, not_1_out, not_2_out, not_3_out, Opcode[0]);
  and and_21 (and_21_out, Opcode[3], not_2_out, Opcode[1], Opcode[0]);
  and and_22 (Lw, not_1_out, Opcode[2], Opcode[1], Opcode[0]);
  and and_23 (Sw, Opcode[3], not_2_out, not_3_out, not_4_out);
  and and_24 (RamToReg, not_1_out, Opcode[2], Opcode[1], Opcode[0]);
  and and_25 (and_25_out, not_1_out, Opcode[2], Opcode[1], Opcode[0]);
  and and_26 (and_26_out, Opcode[3], not_3_out, not_4_out);
  and and_27 (and_27_out, Opcode[3], not_2_out, Opcode[1], Opcode[0]);
  and and_28 (and_28_out, Opcode[3], Opcode[2], not_3_out);
  and and_29 (and_29_out, Opcode[3], Opcode[2], not_4_out);
  and and_30 (Add_Br, Opcode[3], not_2_out, Opcode[1], Opcode[0]);
  and and_31 (Jump, Opcode[3], Opcode[2], Opcode[1], not_4_out);
  and and_32 (Inp, Opcode[3], not_2_out, not_3_out, Opcode[0]);
  and and_33 (Outp, Opcode[3], not_2_out, Opcode[1], not_4_out);
  and and_34 (Sll2[1], Opcode[3], not_2_out, Opcode[1], Opcode[0]);
  or or_1 (RegWrite, not_1_out, and_1_out, and_2_out);
  or or_2 (AluSrc, and_3_out, and_4_out, and_5_out, and_6_out);
  or or_3 (AluOp[3], and_7_out, and_8_out);
  or or_4 (AluOp[2], and_9_out, and_10_out);
  or or_5 (AluOp[1], and_11_out, and_12_out, and_13_out, and_14_out, and_15_out);
  or or_6 (AluOp[0], and_16_out, and_17_out);
  or or_7 (Cin, and_18_out, and_19_out);
  or or_8 (Bin, and_20_out, and_21_out);
  or or_9 (Read_Dest, and_25_out, and_26_out, and_27_out, and_28_out, and_29_out);

  assign Def_Reg = 4'b0110;
  assign {Sll2[3:2], Sll2[0]} = 3'b000;
endmodule

module Full_DataPath (
  input  [11:0] in_1,
  input  Over_Flow,
  input  in_3,
  input  [3:0] in_4,
  input  [11:0] in_5,
  output [3:0] RD,
  output [3:0] RS,
  output [11:0] out_8,
  output [11:0] out_9,
  output [11:0] out_10
);

  wire alu_1_zero, and_1_out, Clockk_out, control_unit_1_add_br, control_unit_1_alusrc, control_unit_1_bin,
       control_unit_1_cin, control_unit_1_inp, control_unit_1_jump, control_unit_1_lw, control_unit_1_outp,
       control_unit_1_ramtoreg, control_unit_1_read_dest, control_unit_1_regwrite, control_unit_1_sw;
  wire [3:0] control_unit_1_aluop, control_unit_1_def_reg, control_unit_1_sll2, multiplexer_2_out,
       multiplexer_4_out;
  wire [7:0] adder_2_out, bit_extender_1_out, bit_extender_2_out, shifter_1_out;
  wire [11:0] adder_1_out, adder_3_out, bit_extender_4_out, demultiplexer_1_out0, demultiplexer_1_out1,
       multiplexer_1_out, multiplexer_3_out, multiplexer_5_out, multiplexer_6_out, multiplexer_7_out,
       ram_1_dout, register_1_q, register_file_1_read_data_2;
  wire [11:8] rom_1_data;

  Multiplexer #(.width(12)) multiplexer_1 (
    .in0(multiplexer_6_out), .in1(bit_extender_4_out), .out(multiplexer_1_out), .sel(control_unit_1_jump));
  Register #(.width(12)) register_1 (
    .D(multiplexer_1_out), .Q(register_1_q), .clk(Clockk_out), .clr(in_3));  // open: en
  Clock Clockk (.out(Clockk_out));
  ROM #(.addrWidth(12), .dataWidth(12)) rom_1 (.addr(register_1_q), .data({rom_1_data, RS, RD}));
  Control_Unit control_unit_1 (
    .Opcode(rom_1_data), .Def_Reg(control_unit_1_def_reg), .RegWrite(control_unit_1_regwrite),
    .AluSrc(control_unit_1_alusrc), .AluOp(control_unit_1_aluop), .Cin(control_unit_1_cin),
    .Bin(control_unit_1_bin), .Lw(control_unit_1_lw), .Sw(control_unit_1_sw),
    .RamToReg(control_unit_1_ramtoreg), .Read_Dest(control_unit_1_read_dest), .Add_Br(control_unit_1_add_br),
    .Jump(control_unit_1_jump), .Inp(control_unit_1_inp), .Outp(control_unit_1_outp),
    .Sll2(control_unit_1_sll2));
  Adder #(.width(12)) adder_1 (.a(register_1_q), .b(in_1), .out(adder_1_out));  // open: cin, cout
  Multiplexer #(.width(4)) multiplexer_2 (.in0(RS), .in1(in_4), .out(multiplexer_2_out), .sel(control_unit_1_inp));
  Multiplexer #(.width(12)) multiplexer_3 (
    .in0(in_5), .in1(multiplexer_7_out), .out(multiplexer_3_out), .sel(control_unit_1_inp));
  assign bit_extender_1_out = {{4{RS[3]}}, RS};  // Bit_Extender bit_extender_1
  Multiplexer #(.width(4)) multiplexer_4 (
    .in0(RD), .in1(control_unit_1_def_reg), .out(multiplexer_4_out), .sel(control_unit_1_read_dest));
  Shifter shifter_1 (.in(bit_extender_1_out), .\dist (3'b100), .out(shifter_1_out));
  Register_File register_file_1 (
    .Read_Reg_1(RS), .Read_reg_2(multiplexer_4_out), .Clock(Clockk_out), .enable(control_unit_1_regwrite),
    .Data_Input(multiplexer_3_out), .write_reg(multiplexer_2_out), .Read_data_1(out_8),
    .Read_Data_2(register_file_1_read_data_2));
  assign bit_extender_2_out = {{4{RD[3]}}, RD};  // Bit_Extender bit_extender_2
  assign out_9 = {{8{RD[3]}}, RD};  // Bit_Extender bit_extender_3
  Adder adder_2 (.a(bit_extender_2_out), .b(shifter_1_out), .out(adder_2_out));  // open: cin, cout
  Demultiplexer #(.width(12)) demultiplexer_1 (
    .out0(demultiplexer_1_out0), .out1(demultiplexer_1_out1), .in(out_8), .sel(control_unit_1_outp));
  assign bit_extender_4_out = {{4{adder_2_out[7]}}, adder_2_out};  // Bit_Extender bit_extender_4
  Multiplexer #(.width(12)) multiplexer_5 (
    .in0(register_file_1_read_data_2), .in1(out_9), .out(multiplexer_5_out), .sel(control_unit_1_alusrc));
  alu alu_1 (
    .Cin(control_unit_1_cin), .B_Inv(control_unit_1_bin), .A(demultiplexer_1_out0), .B(multiplexer_5_out),
    .ALU_OP(control_unit_1_aluop), .out_6(Over_Flow), .RES(out_10), .zero(alu_1_zero));
  RAM #(.addrWidth(12), .dataWidth(12)) ram_1 (
    .addr(out_10), .we(control_unit_1_sw), .oe(control_unit_1_lw), .clk(Clockk_out),
    .din(register_file_1_read_data_2), .dout(ram_1_dout));
  Adder #(.width(12)) adder_3 (.a(adder_1_out), .b(out_9), .out(adder_3_out));  // open: cin, cout
  Multiplexer #(.width(12)) multiplexer_6 (
    .in0(adder_1_out), .in1(adder_3_out), .out(multiplexer_6_out), .sel(and_1_out));
  and and_1 (and_1_out, control_unit_1_add_br, alu_1_zero);
  Hex_Digit_Display hex_digit_display_1 (.value(demultiplexer_1_out1[3:0]));  // open: dp
  Hex_Digit_Display hex_digit_display_2 (.value(demultiplexer_1_out1[7:4]));  // open: dp
  Hex_Digit_Display hex_digit_display_3 (.value(demultiplexer_1_out1[11:8]));  // open: dp
  Multiplexer #(.width(12)) multiplexer_7 (
    .in0(ram_1_dout), .in1(out_10), .out(multiplexer_7_out), .sel(control_unit_1_ramtoreg));

  // Notes on the sheet:
  //   contents of rom_1 (hex, n*v repeats v):
  //   12 e10
endmodule
